# Fritzing sketch HSU (saved by Fritzing 0.7.11b)
breadboards: 1

parts:
  JY-MCU = Generic female header - 4 pins [package=THT]
  R2 = 10k Ω Resistor [package=THT]
  9V_VCC = Battery block 9V
  S1 = Pushbutton [package="[THT]"]
  R3 = 10k Ω Resistor [package=THT]
  LED2 = RGB LED (com. cathode, rgb) [package="5 mm [THT]"]
  R1 = 10k Ω Resistor [package=THT]
  R4 = 150 Ω Resistor [package=THT]
  R5 = 100 Ω Resistor [package=THT]
  R6 = 100 Ω Resistor [package=THT]
  J1 = Generic female header - 7 pins [package=THT]
  Nano = Arduino Nano v3.0
  S2 = Toggle Switch [package=THT]

nets:
  N1: JY-MCU.pin1, R1.Pin_1
  N2: JY-MCU.pin2, R2.Pin_1
  N3: JY-MCU.pin3, 9V_VCC.-, R3.Pin_1, LED2.common_cathode, J1.pin2, Nano.GND
  N4: JY-MCU.pin4, Nano.D5
  N5: R2.Pin_0, Nano.D2
  N6: 9V_VCC.+, S2.COM
  N7: S1.Pin_1, S1.Pin_2, Nano.+5V
  N8: S1.Pin_3, S1.Pin_4, R3.Pin_0, Nano.D4
  N9: LED2.red_anode, R4.Pin_1
  N10: LED2.green_anode, R5.Pin_1
  N11: LED2.blue_anode, R6.Pin_1
  N12: R1.Pin_0, Nano.D3
  N13: R4.Pin_0, Nano.D6
  N14: R5.Pin_0, Nano.D7
  N15: R6.Pin_0, Nano.D8
  N16: J1.pin1, Nano.3V3
  N17: J1.pin3, Nano.A4
  N18: J1.pin4, Nano.A5
  N19: Nano.VIN, S2.L1

notes:
  HSU Main Board v1.0
  JY-MCU Width = 16.04 mm
  JY-MCU Height = 36.12 mm
