# Fritzing sketch HSUSensor (saved by Fritzing 0.7.10b)
breadboards: 1

parts:
  J1 = Generic male header - 7 pins [package=THT]
  MLX90614 = MLX90614 Infrared Thermometer
  R1 = Resistor [tolerance=±5% resistance=4.7k package=THT]
  R2 = Resistor [tolerance=±5% resistance=4.7k package=THT]
  C1 = Ceramic Capacitor [capacitance=0.1µF package="100 mil [THT, multilayer]"]

nets:
  N1: J1.pin1, MLX90614.VDD, R1.Pin_0, R2.Pin_0, C1.0
  N2: J1.pin2, MLX90614.VSS, C1.1
  N3: J1.pin3, MLX90614.SCL_/_Vz, R2.Pin_1
  N4: J1.pin4, MLX90614.PWM_/_SDA, R1.Pin_1

notes:
  HSU Sensor Board v1.0

custom parts:
  MLX90614 Infrared Thermometer: The MLX90614 is an Infra Red thermometer for non contact temperature measurements. Both the IR sensitive thermopile detector chip and the signal conditioning ASSP are integrated in the same TO-39 can.
