# Fritzing sketch TCHandScanner (saved by Fritzing 0.7.11b)
breadboards: 1

parts:
  Nano = Arduino Nano v3.0
  JY-MCU = Generic female header - 4 pins [package=THT]
  R1 = 10k Ω Resistor [package=THT]
  R2 = 10k Ω Resistor [package=THT]
  VCC_(9V) = Battery block 9V

nets:
  N1: Nano.GND, JY-MCU.pin3, VCC_(9V).-
  N2: Nano.D2, R2.Pin_0
  N3: Nano.D3, R1.Pin_0
  N4: Nano.+5V, JY-MCU.pin4
  N5: Nano.VIN, VCC_(9V).+
  N6: JY-MCU.pin1, R1.Pin_1
  N7: JY-MCU.pin2, R2.Pin_1
